# Fritzing sketch thermrf (saved by Fritzing 0.7.10b)
breadboards: 1

parts:
  Arduino1 = Arduino
  R1 = Resistor [tolerance=±5% resistance=1k package=THT]
  R3 = Resistor [tolerance=±5% resistance=1k package=THT]
  IC1 = IC, DIP package, 8 pins [chip_label=DS1634]

nets:
  N1: Arduino1.+5V, R1.Pin_0, R3.Pin_0, IC1.pin8
  N2: Arduino1.A4, R3.Pin_1, IC1.pin1
  N3: Arduino1.A5, R1.Pin_1, IC1.pin2
  N4: IC1.pin4, IC1.pin5, IC1.pin6, IC1.pin7
